// Logisim project Atividade09.circ as structural Verilog: 2 circuits, main circuit Todos
module main (
  input  in_1,
  input  in_2,
  input  in_3,
  output out_4,
  output out_5
);

  wire and_1_out, and_2_out, and_3_out, xor_1_out;

  xor xor_1 (xor_1_out, in_1, in_2);
  and and_1 (and_1_out, in_2, in_3);
  and and_2 (and_2_out, in_3, in_1);
  and and_3 (and_3_out, in_2, in_1);
  xor xor_2 (out_4, xor_1_out, in_3);
  or or_1 (out_5, and_1_out, and_2_out, and_3_out);
endmodule

module Todos (
  input  in_1
);

  wire dipswitch_1_p1, dipswitch_1_p2, dipswitch_1_p3, dipswitch_1_p4, dipswitch_1_p5, dipswitch_1_p6,
       dipswitch_1_p7, dipswitch_1_p8, dipswitch_2_p1, dipswitch_2_p2, dipswitch_2_p3, dipswitch_2_p4,
       dipswitch_2_p5, dipswitch_2_p6, dipswitch_2_p7, dipswitch_2_p8, main_1_out_4, main_1_out_5,
       main_2_out_4, main_2_out_5, main_3_out_4, main_3_out_5, main_4_out_4, main_4_out_5, main_5_out_4,
       main_5_out_5, main_6_out_4, main_6_out_5, main_7_out_4, main_7_out_5, main_8_out_4, main_8_out_5,
       xor_1_out, xor_2_out, xor_3_out, xor_4_out, xor_5_out, xor_6_out, xor_7_out, xor_8_out;

  LED led_1 (.in(main_1_out_5));
  xor xor_1 (xor_1_out, dipswitch_2_p8, in_1);
  main main_1 (
    .out_5(main_1_out_5), .out_4(main_1_out_4), .in_1(main_2_out_5), .in_2(dipswitch_1_p8), .in_3(xor_1_out));
  LED led_2 (.in(main_1_out_4));
  // DipSwitch dipswitch_1: pin names not known; wires that end beside it: dipswitch_1_p1, dipswitch_1_p2, dipswitch_1_p3, dipswitch_1_p4, dipswitch_1_p5, dipswitch_1_p6, dipswitch_1_p7, dipswitch_1_p8
  xor xor_2 (xor_2_out, dipswitch_2_p7, in_1);
  main main_2 (
    .out_5(main_2_out_5), .out_4(main_2_out_4), .in_1(main_3_out_5), .in_2(dipswitch_1_p7), .in_3(xor_2_out));
  LED led_3 (.in(main_2_out_4));
  xor xor_3 (xor_3_out, dipswitch_2_p6, in_1);
  main main_3 (
    .out_5(main_3_out_5), .out_4(main_3_out_4), .in_1(main_4_out_5), .in_2(dipswitch_1_p6), .in_3(xor_3_out));
  LED led_4 (.in(main_3_out_4));
  xor xor_4 (xor_4_out, dipswitch_2_p5, in_1);
  main main_4 (
    .out_5(main_4_out_5), .out_4(main_4_out_4), .in_1(main_5_out_5), .in_2(dipswitch_1_p5), .in_3(xor_4_out));
  LED led_5 (.in(main_4_out_4));
  xor xor_5 (xor_5_out, dipswitch_2_p4, in_1);
  main main_5 (
    .out_5(main_5_out_5), .out_4(main_5_out_4), .in_1(main_6_out_5), .in_2(dipswitch_1_p4), .in_3(xor_5_out));
  LED led_6 (.in(main_5_out_4));
  xor xor_6 (xor_6_out, dipswitch_2_p3, in_1);
  main main_6 (
    .out_5(main_6_out_5), .out_4(main_6_out_4), .in_1(main_7_out_5), .in_2(dipswitch_1_p3), .in_3(xor_6_out));
  LED led_7 (.in(main_6_out_4));
  main main_7 (
    .out_5(main_7_out_5), .out_4(main_7_out_4), .in_1(main_8_out_5), .in_2(dipswitch_1_p2), .in_3(xor_7_out));
  LED led_8 (.in(main_7_out_4));
  xor xor_7 (xor_7_out, dipswitch_2_p2, in_1);
  // DipSwitch dipswitch_2: pin names not known; wires that end beside it: dipswitch_2_p1, dipswitch_2_p2, dipswitch_2_p3, dipswitch_2_p4, dipswitch_2_p5, dipswitch_2_p6, dipswitch_2_p7, dipswitch_2_p8
  xor xor_8 (xor_8_out, dipswitch_2_p1, in_1);
  main main_8 (.out_5(main_8_out_5), .out_4(main_8_out_4), .in_1(in_1), .in_2(dipswitch_1_p1), .in_3(xor_8_out));
  LED led_9 (.in(main_8_out_4));
endmodule
