// Logisim project BatalhaNaval.circ as structural Verilog
module A0000 (
  input  A,
  input  B,
  input  C,
  input  D,
  input  A1,
  input  B1,
  input  C1,
  input  D1,
  input  in_9,
  input  in_10,
  input  in_11,
  input  in_12,
  output out_13,
  output out_14
);

  wire and_1_out, and_2_out, and_3_out, not_1_out, not_2_out, not_3_out, not_4_out;

  not not_1 (not_1_out, A);
  not not_2 (not_2_out, B);
  not not_3 (not_3_out, C);
  not not_4 (not_4_out, D);
  and and_1 (and_1_out, not_1_out, not_2_out, not_3_out, not_4_out);
  and and_2 (and_2_out, A1, B1, C1, D1);
  and and_3 (and_3_out, in_9, in_10, in_11, in_12);
  and and_4 (out_13, and_1_out, and_2_out);
  and and_5 (out_14, and_1_out, and_3_out);
endmodule

module A0001 (
  input  A,
  input  B,
  input  C,
  input  D,
  input  A1,
  input  B1,
  input  C1,
  input  D1,
  input  in_9,
  input  in_10,
  input  in_11,
  input  in_12,
  output out_13,
  output out_14
);

  wire and_1_out, and_2_out, and_3_out, not_1_out, not_2_out, not_3_out, not_4_out, not_5_out, not_6_out,
       not_7_out;

  not not_1 (not_1_out, A);
  not not_2 (not_2_out, B);
  not not_3 (not_3_out, C);
  not not_4 (not_4_out, A1);
  not not_5 (not_5_out, C1);
  not not_6 (not_6_out, in_9);
  not not_7 (not_7_out, in_11);
  and and_1 (and_1_out, not_1_out, not_2_out, not_3_out, D);
  and and_2 (and_2_out, not_4_out, B1, not_5_out, D1);
  and and_3 (and_3_out, not_6_out, in_10, not_7_out, in_12);
  and and_4 (out_13, and_1_out, and_2_out);
  and and_5 (out_14, and_1_out, and_3_out);
endmodule

module A0010 (
  input  A,
  input  B,
  input  C,
  input  D,
  input  A1,
  input  B1,
  input  C1,
  input  D1,
  input  in_9,
  input  in_10,
  input  in_11,
  input  in_12,
  output out_13,
  output out_14
);

  wire and_1_out, and_2_out, and_3_out, not_1_out, not_2_out, not_3_out, not_4_out, not_5_out, not_6_out,
       not_7_out, not_8_out, not_9_out;

  not not_1 (not_1_out, A);
  not not_2 (not_2_out, B);
  not not_3 (not_3_out, D);
  not not_4 (not_4_out, A1);
  not not_5 (not_5_out, B1);
  not not_6 (not_6_out, D1);
  not not_7 (not_7_out, in_9);
  not not_8 (not_8_out, in_10);
  not not_9 (not_9_out, in_12);
  and and_1 (and_1_out, not_1_out, not_2_out, C, not_3_out);
  and and_2 (and_2_out, not_4_out, not_5_out, C1, not_6_out);
  and and_3 (and_3_out, not_7_out, not_8_out, in_11, not_9_out);
  and and_4 (out_13, and_1_out, and_2_out);
  and and_5 (out_14, and_1_out, and_3_out);
endmodule

module A0011 (
  input  A,
  input  B,
  input  C,
  input  D,
  input  A1,
  input  B1,
  input  C1,
  input  D1,
  input  in_9,
  input  in_10,
  input  in_11,
  input  in_12,
  output out_13,
  output out_14
);

  wire and_1_out, and_2_out, and_3_out, not_1_out, not_2_out, not_3_out, not_4_out, not_5_out, not_6_out,
       not_7_out, not_8_out, not_9_out, not_10_out;

  not not_1 (not_1_out, A);
  not not_2 (not_2_out, B);
  not not_3 (not_3_out, A1);
  not not_4 (not_4_out, B1);
  not not_5 (not_5_out, C1);
  not not_6 (not_6_out, D1);
  not not_7 (not_7_out, in_9);
  not not_8 (not_8_out, in_10);
  not not_9 (not_9_out, in_11);
  not not_10 (not_10_out, in_12);
  and and_1 (and_1_out, not_1_out, not_2_out, C, D);
  and and_2 (and_2_out, not_3_out, not_4_out, not_5_out, not_6_out);
  and and_3 (and_3_out, not_7_out, not_8_out, not_9_out, not_10_out);
  and and_4 (out_13, and_1_out, and_2_out);
  and and_5 (out_14, and_1_out, and_3_out);
endmodule

module A0100 (
  input  A,
  input  B,
  input  C,
  input  D,
  input  A1,
  input  B1,
  input  C1,
  input  D1,
  input  in_9,
  input  in_10,
  input  in_11,
  input  in_12,
  output out_13,
  output out_14
);

  wire and_1_out, and_2_out, and_3_out, not_1_out, not_2_out, not_3_out, not_4_out, not_5_out;

  not not_1 (not_1_out, A);
  not not_2 (not_2_out, C);
  not not_3 (not_3_out, D);
  not not_4 (not_4_out, D1);
  not not_5 (not_5_out, in_12);
  and and_1 (and_1_out, not_1_out, B, not_2_out, not_3_out);
  and and_2 (and_2_out, A1, B1, C1, not_4_out);
  and and_3 (and_3_out, in_9, in_10, in_11, not_5_out);
  and and_4 (out_13, and_1_out, and_2_out);
  and and_5 (out_14, and_1_out, and_3_out);
endmodule

module A0101 (
  input  A,
  input  B,
  input  C,
  input  D,
  input  A1,
  input  B1,
  input  C1,
  input  D1,
  input  in_9,
  input  in_10,
  input  in_11,
  input  in_12,
  output out_13,
  output out_14
);

  wire and_1_out, and_2_out, and_3_out, not_1_out, not_2_out, not_3_out, not_4_out, not_5_out, not_6_out,
       not_7_out, not_8_out;

  not not_1 (not_1_out, A);
  not not_2 (not_2_out, C);
  not not_3 (not_3_out, B1);
  not not_4 (not_4_out, C1);
  not not_5 (not_5_out, D1);
  not not_6 (not_6_out, in_10);
  not not_7 (not_7_out, in_11);
  not not_8 (not_8_out, in_12);
  and and_1 (and_1_out, not_1_out, B, not_2_out, D);
  and and_2 (and_2_out, A1, not_3_out, not_4_out, not_5_out);
  and and_3 (and_3_out, in_9, not_6_out, not_7_out, not_8_out);
  and and_4 (out_13, and_1_out, and_2_out);
  and and_5 (out_14, and_1_out, and_3_out);
endmodule

module A0110 (
  input  A,
  input  B,
  input  C,
  input  D,
  input  A1,
  input  B1,
  input  C1,
  input  D1,
  input  in_9,
  input  in_10,
  input  in_11,
  input  in_12,
  output out_13,
  output out_14
);

  wire and_1_out, and_2_out, and_3_out, not_1_out, not_2_out, not_3_out, not_4_out, not_5_out, not_6_out,
       not_7_out, not_8_out;

  not not_1 (not_1_out, A);
  not not_2 (not_2_out, D);
  not not_3 (not_3_out, A1);
  not not_4 (not_4_out, C1);
  not not_5 (not_5_out, D1);
  not not_6 (not_6_out, in_9);
  not not_7 (not_7_out, in_11);
  not not_8 (not_8_out, in_12);
  and and_1 (and_1_out, not_1_out, B, C, not_2_out);
  and and_2 (and_2_out, not_3_out, B1, not_4_out, not_5_out);
  and and_3 (and_3_out, not_6_out, in_10, not_7_out, not_8_out);
  and and_4 (out_13, and_1_out, and_2_out);
  and and_5 (out_14, and_1_out, and_3_out);
endmodule

module A0111 (
  input  A,
  input  B,
  input  C,
  input  D,
  input  A1,
  input  B1,
  input  C1,
  input  D1,
  input  in_9,
  input  in_10,
  input  in_11,
  input  in_12,
  output out_13,
  output out_14
);

  wire and_1_out, and_2_out, and_3_out, not_1_out, not_2_out, not_3_out, not_4_out, not_5_out;

  not not_1 (not_1_out, A);
  not not_2 (not_2_out, A1);
  not not_3 (not_3_out, B1);
  not not_4 (not_4_out, in_9);
  not not_5 (not_5_out, in_10);
  and and_1 (and_1_out, not_1_out, B, C, D);
  and and_2 (and_2_out, not_2_out, not_3_out, C1, D1);
  and and_3 (and_3_out, not_4_out, not_5_out, in_11, in_12);
  and and_4 (out_13, and_1_out, and_2_out);
  and and_5 (out_14, and_1_out, and_3_out);
endmodule

module A1000 (
  input  A,
  input  B,
  input  C,
  input  D,
  input  A1,
  input  B1,
  input  C1,
  input  D1,
  input  in_9,
  input  in_10,
  input  in_11,
  input  in_12,
  output out_13,
  output out_14
);

  wire and_1_out, and_2_out, and_3_out, not_1_out, not_2_out, not_3_out, not_4_out, not_5_out;

  not not_1 (not_1_out, B);
  not not_2 (not_2_out, C);
  not not_3 (not_3_out, D);
  not not_4 (not_4_out, C1);
  not not_5 (not_5_out, in_11);
  and and_1 (and_1_out, A, not_1_out, not_2_out, not_3_out);
  and and_2 (and_2_out, A1, B1, not_4_out, D1);
  and and_3 (and_3_out, in_9, in_10, not_5_out, in_12);
  and and_4 (out_13, and_1_out, and_2_out);
  and and_5 (out_14, and_1_out, and_3_out);
endmodule

module A1001 (
  input  A,
  input  B,
  input  C,
  input  D,
  input  A1,
  input  B1,
  input  C1,
  input  D1,
  input  in_9,
  input  in_10,
  input  in_11,
  input  in_12,
  output out_13,
  output out_14
);

  wire and_1_out, and_2_out, and_3_out, not_1_out, not_2_out, not_3_out, not_4_out;

  not not_1 (not_1_out, B);
  not not_2 (not_2_out, C);
  not not_3 (not_3_out, A1);
  not not_4 (not_4_out, in_9);
  and and_1 (and_1_out, A, not_1_out, not_2_out, D);
  and and_2 (and_2_out, not_3_out, B1, C1, D1);
  and and_3 (and_3_out, not_4_out, in_10, in_11, in_12);
  and and_4 (out_13, and_1_out, and_2_out);
  and and_5 (out_14, and_1_out, and_3_out);
endmodule

module A1010 (
  input  A,
  input  B,
  input  C,
  input  D,
  input  A1,
  input  B1,
  input  C1,
  input  D1,
  input  in_9,
  input  in_10,
  input  in_11,
  input  in_12,
  output out_13,
  output out_14
);

  wire and_1_out, and_2_out, and_3_out, not_1_out, not_2_out, not_3_out, not_4_out, not_5_out, not_6_out;

  not not_1 (not_1_out, B);
  not not_2 (not_2_out, D);
  not not_3 (not_3_out, C1);
  not not_4 (not_4_out, D1);
  not not_5 (not_5_out, in_11);
  not not_6 (not_6_out, in_12);
  and and_1 (and_1_out, A, not_1_out, C, not_2_out);
  and and_2 (and_2_out, A1, B1, not_3_out, not_4_out);
  and and_3 (and_3_out, in_9, in_10, not_5_out, not_6_out);
  and and_4 (out_13, and_1_out, and_2_out);
  and and_5 (out_14, and_1_out, and_3_out);
endmodule

module A1011 (
  input  A,
  input  B,
  input  C,
  input  D,
  input  A1,
  input  B1,
  input  C1,
  input  D1,
  input  in_9,
  input  in_10,
  input  in_11,
  input  in_12,
  output out_13,
  output out_14
);

  wire and_1_out, and_2_out, and_3_out, not_1_out, not_2_out, not_3_out, not_4_out, not_5_out, not_6_out,
       not_7_out;

  not not_1 (not_1_out, B);
  not not_2 (not_2_out, A1);
  not not_3 (not_3_out, B1);
  not not_4 (not_4_out, C1);
  not not_5 (not_5_out, in_9);
  not not_6 (not_6_out, in_10);
  not not_7 (not_7_out, in_11);
  and and_1 (and_1_out, A, not_1_out, C, D);
  and and_2 (and_2_out, not_2_out, not_3_out, not_4_out, D1);
  and and_3 (and_3_out, not_5_out, not_6_out, not_7_out, in_12);
  and and_4 (out_13, and_1_out, and_2_out);
  and and_5 (out_14, and_1_out, and_3_out);
endmodule

module A1100 (
  input  A,
  input  B,
  input  C,
  input  D,
  input  A1,
  input  B1,
  input  C1,
  input  D1,
  input  in_9,
  input  in_10,
  input  in_11,
  input  in_12,
  output out_13,
  output out_14
);

  wire and_1_out, and_2_out, and_3_out, not_1_out, not_2_out, not_3_out, not_4_out;

  not not_1 (not_1_out, C);
  not not_2 (not_2_out, D);
  not not_3 (not_3_out, B1);
  not not_4 (not_4_out, in_10);
  and and_1 (and_1_out, A, B, not_1_out, not_2_out);
  and and_2 (and_2_out, A1, not_3_out, C1, D1);
  and and_3 (and_3_out, in_9, not_4_out, in_11, in_12);
  and and_4 (out_13, and_1_out, and_2_out);
  and and_5 (out_14, and_1_out, and_3_out);
endmodule

module A1101 (
  input  A,
  input  B,
  input  C,
  input  D,
  input  A1,
  input  B1,
  input  C1,
  input  D1,
  input  in_9,
  input  in_10,
  input  in_11,
  input  in_12,
  output out_13,
  output out_14
);

  wire and_1_out, and_2_out, and_3_out, not_1_out, not_2_out, not_3_out, not_4_out, not_5_out;

  not not_1 (not_1_out, C);
  not not_2 (not_2_out, C1);
  not not_3 (not_3_out, in_9);
  not not_4 (not_4_out, in_11);
  not not_5 (not_5_out, A1);
  and and_1 (and_1_out, A, B, not_1_out, D);
  and and_2 (and_2_out, not_5_out, B1, not_2_out, D1);
  and and_3 (and_3_out, not_3_out, in_10, not_4_out, in_12);
  and and_4 (out_13, and_1_out, and_2_out);
  and and_5 (out_14, and_1_out, and_3_out);
endmodule

module A1110 (
  input  A,
  input  B,
  input  C,
  input  D,
  input  A1,
  input  B1,
  input  C1,
  input  D1,
  input  in_9,
  input  in_10,
  input  in_11,
  input  in_12,
  output out_13,
  output out_14
);

  wire and_1_out, and_2_out, and_3_out, not_1_out, not_2_out, not_3_out, not_4_out, not_5_out;

  not not_1 (not_1_out, D);
  not not_2 (not_2_out, A1);
  not not_3 (not_3_out, D1);
  not not_4 (not_4_out, in_9);
  not not_5 (not_5_out, in_12);
  and and_1 (and_1_out, A, B, C, not_1_out);
  and and_2 (and_2_out, not_2_out, B1, C1, not_3_out);
  and and_3 (and_3_out, not_4_out, in_10, in_11, not_5_out);
  and and_4 (out_13, and_1_out, and_2_out);
  and and_5 (out_14, and_1_out, and_3_out);
endmodule

module A1111 (
  input  A,
  input  B,
  input  C,
  input  D,
  input  A1,
  input  B1,
  input  C1,
  input  D1,
  input  in_9,
  input  in_10,
  input  in_11,
  input  in_12,
  output out_13,
  output out_14
);

  wire and_1_out, and_2_out, and_3_out, not_1_out, not_2_out, not_3_out, not_4_out;

  not not_1 (not_1_out, B1);
  not not_2 (not_2_out, C1);
  not not_3 (not_3_out, in_10);
  not not_4 (not_4_out, in_11);
  and and_1 (and_1_out, A, B, C, D);
  and and_2 (and_2_out, A1, not_1_out, not_2_out, D1);
  and and_3 (and_3_out, in_9, not_3_out, not_4_out, in_12);
  and and_4 (out_13, and_1_out, and_2_out);
  and and_5 (out_14, and_1_out, and_3_out);
endmodule

module TODOS (
  input  in_1,
  input  in_2,
  input  in_3,
  input  in_4,
  input  in_5,
  input  in_6,
  input  in_7,
  input  in_8,
  input  in_9,
  input  in_10,
  input  in_11,
  input  in_12,
  output out_13,
  output out_14
);

  wire a0000_1_out_13, a0000_1_out_14, a0001_1_out_13, a0001_1_out_14, a0010_1_out_13, a0010_1_out_14,
       a0011_1_out_13, a0011_1_out_14, a0100_1_out_13, a0100_1_out_14, a0101_1_out_13, a0101_1_out_14,
       a0110_1_out_13, a0110_1_out_14, a0111_1_out_13, a0111_1_out_14, a1000_1_out_13, a1000_1_out_14,
       a1001_1_out_13, a1001_1_out_14, a1010_1_out_13, a1010_1_out_14, a1011_1_out_13, a1011_1_out_14,
       a1100_1_out_13, a1100_1_out_14, a1101_1_out_13, a1101_1_out_14, a1110_1_out_13, a1110_1_out_14,
       a1111_1_out_13, a1111_1_out_14;

  A0000 a0000_1 (
    .out_13(a0000_1_out_13), .out_14(a0000_1_out_14), .B(in_3), .C(in_2), .D(in_1), .A1(in_5), .B1(in_6),
    .C1(in_7), .D1(in_8), .in_9(in_9), .A(in_4), .in_10(in_10), .in_11(in_11), .in_12(in_12));
  A0100 a0100_1 (
    .A(in_4), .B(in_3), .C(in_2), .D(in_1), .A1(in_5), .B1(in_6), .C1(in_7), .D1(in_8), .in_9(in_9),
    .in_10(in_10), .in_11(in_11), .in_12(in_12), .out_13(a0100_1_out_13), .out_14(a0100_1_out_14));
  A1000 a1000_1 (
    .A(in_4), .B(in_3), .C(in_2), .D(in_1), .A1(in_5), .B1(in_6), .C1(in_7), .D1(in_8), .in_9(in_9),
    .in_10(in_10), .in_11(in_11), .in_12(in_12), .out_13(a1000_1_out_13), .out_14(a1000_1_out_14));
  A1100 a1100_1 (
    .A(in_4), .B(in_3), .C(in_2), .D(in_1), .A1(in_5), .B1(in_6), .C1(in_7), .D1(in_8), .in_9(in_9),
    .in_10(in_10), .in_11(in_11), .in_12(in_12), .out_13(a1100_1_out_13), .out_14(a1100_1_out_14));
  A0001 a0001_1 (
    .A(in_4), .B(in_3), .C(in_2), .D(in_1), .A1(in_5), .B1(in_6), .C1(in_7), .D1(in_8), .in_9(in_9),
    .in_10(in_10), .in_11(in_11), .in_12(in_12), .out_13(a0001_1_out_13), .out_14(a0001_1_out_14));
  A0101 a0101_1 (
    .A(in_4), .B(in_3), .C(in_2), .D(in_1), .A1(in_5), .B1(in_6), .C1(in_7), .D1(in_8), .in_9(in_9),
    .in_10(in_10), .in_11(in_11), .in_12(in_12), .out_13(a0101_1_out_13), .out_14(a0101_1_out_14));
  A1001 a1001_1 (
    .A(in_4), .B(in_3), .C(in_2), .D(in_1), .A1(in_5), .B1(in_6), .C1(in_7), .D1(in_8), .in_9(in_9),
    .in_10(in_10), .in_11(in_11), .in_12(in_12), .out_13(a1001_1_out_13), .out_14(a1001_1_out_14));
  A1101 a1101_1 (
    .A(in_4), .B(in_3), .C(in_2), .D(in_1), .A1(in_5), .B1(in_6), .C1(in_7), .D1(in_8), .in_9(in_9),
    .in_10(in_10), .in_11(in_11), .in_12(in_12), .out_13(a1101_1_out_13), .out_14(a1101_1_out_14));
  or or_1 (out_13, a1100_1_out_14, a1100_1_out_13, a1000_1_out_14, a1000_1_out_13, a0100_1_out_14, a0100_1_out_13, a0000_1_out_14, a0000_1_out_13, a1101_1_out_14, a1101_1_out_13, a1001_1_out_14, a1001_1_out_13, a0101_1_out_14, a0101_1_out_13, a0001_1_out_14, a0001_1_out_13, a0011_1_out_13, a0011_1_out_14, a0111_1_out_13, a0111_1_out_14, a1011_1_out_13, a1011_1_out_14, a1111_1_out_13, a1111_1_out_14, a0010_1_out_13, a0010_1_out_14, a0110_1_out_13, a0110_1_out_14, a1010_1_out_13, a1010_1_out_14, a1110_1_out_13, a1110_1_out_14);
  not not_1 (out_14, out_13);
  A0010 a0010_1 (
    .A(in_4), .B(in_3), .C(in_2), .D(in_1), .A1(in_5), .B1(in_6), .C1(in_7), .D1(in_8), .in_9(in_9),
    .in_10(in_10), .in_11(in_11), .in_12(in_12), .out_13(a0010_1_out_13), .out_14(a0010_1_out_14));
  A0110 a0110_1 (
    .A(in_4), .B(in_3), .C(in_2), .D(in_1), .A1(in_5), .B1(in_6), .C1(in_7), .D1(in_8), .in_9(in_9),
    .in_10(in_10), .in_11(in_11), .in_12(in_12), .out_13(a0110_1_out_13), .out_14(a0110_1_out_14));
  A1010 a1010_1 (
    .A(in_4), .B(in_3), .C(in_2), .D(in_1), .A1(in_5), .B1(in_6), .C1(in_7), .D1(in_8), .in_9(in_9),
    .in_10(in_10), .in_11(in_11), .in_12(in_12), .out_13(a1010_1_out_13), .out_14(a1010_1_out_14));
  A1110 a1110_1 (
    .A(in_4), .B(in_3), .C(in_2), .D(in_1), .A1(in_5), .B1(in_6), .C1(in_7), .D1(in_8), .in_9(in_9),
    .in_10(in_10), .in_11(in_11), .in_12(in_12), .out_13(a1110_1_out_13), .out_14(a1110_1_out_14));
  A0011 a0011_1 (
    .A(in_4), .B(in_3), .C(in_2), .D(in_1), .A1(in_5), .B1(in_6), .C1(in_7), .D1(in_8), .in_9(in_9),
    .in_10(in_10), .in_11(in_11), .in_12(in_12), .out_13(a0011_1_out_13), .out_14(a0011_1_out_14));
  A0111 a0111_1 (
    .A(in_4), .B(in_3), .C(in_2), .D(in_1), .A1(in_5), .B1(in_6), .C1(in_7), .D1(in_8), .in_9(in_9),
    .in_10(in_10), .in_11(in_11), .in_12(in_12), .out_13(a0111_1_out_13), .out_14(a0111_1_out_14));
  A1011 a1011_1 (
    .A(in_4), .B(in_3), .C(in_2), .D(in_1), .A1(in_5), .B1(in_6), .C1(in_7), .D1(in_8), .in_9(in_9),
    .in_10(in_10), .in_11(in_11), .in_12(in_12), .out_13(a1011_1_out_13), .out_14(a1011_1_out_14));
  A1111 a1111_1 (
    .A(in_4), .B(in_3), .C(in_2), .D(in_1), .A1(in_5), .B1(in_6), .C1(in_7), .D1(in_8), .in_9(in_9),
    .in_10(in_10), .in_11(in_11), .in_12(in_12), .out_13(a1111_1_out_13), .out_14(a1111_1_out_14));
endmodule

module batalha (
  output out_1,
  output out_2
);

  wire button_1_out, dipswitch_1_p1, dipswitch_1_p2, dipswitch_1_p3, dipswitch_2_p1, dipswitch_2_p2,
       dipswitch_2_p3, dipswitch_2_p4, dipswitch_2_p5, dipswitch_3_p1, dipswitch_3_p2, dipswitch_3_p3,
       dipswitch_3_p4, todos_1_out_13, todos_1_out_14;

  // DipSwitch #(.number(4)) dipswitch_1: pin names not known; wires that end beside it: dipswitch_1_p1, dipswitch_1_p2, dipswitch_1_p3
  // DipSwitch #(.number(4)) dipswitch_2: pin names not known; wires that end beside it: dipswitch_2_p1, dipswitch_2_p2, dipswitch_2_p3, dipswitch_2_p4, dipswitch_2_p5
  and and_1 (out_1, button_1_out, todos_1_out_13);
  TODOS todos_1 (
    .out_13(todos_1_out_13), .out_14(todos_1_out_14), .in_1(dipswitch_3_p1), .in_2(dipswitch_3_p2),
    .in_3(dipswitch_3_p3), .in_4(dipswitch_3_p4), .in_5(dipswitch_1_p1), .in_6(dipswitch_1_p2),
    .in_7(dipswitch_1_p3), .in_8(dipswitch_2_p1), .in_9(dipswitch_2_p2), .in_10(dipswitch_2_p3),
    .in_11(dipswitch_2_p4), .in_12(dipswitch_2_p5));
  and and_2 (out_2, todos_1_out_14, button_1_out);
  // DipSwitch #(.number(4)) dipswitch_3: pin names not known; wires that end beside it: dipswitch_3_p1, dipswitch_3_p2, dipswitch_3_p3, dipswitch_3_p4
  Button button_1 (.out(button_1_out));

  // Notes on the sheet:
  //   ACERTOU
  //   ERROU
  //   DISPARAR
endmodule
